// Logisim project main.circ as structural Verilog: 2 circuits, main circuit main
module main (
);

  wire cdm16_1_p3, cdm16_1_p10, cdm16_1_p12, cdm16_1_p14, clock_1_out, clock_3_out, comparator_1_eq, mem,
       not_1_out, read, word;
  wire [15:0] address_bus, cdm16_1_p20, cdm16_1_p21, data, data_bus, r0, r1, r2, r3, r4, r5, r6, r7,
       random_1_out_2;
  wire [18:0] undriven;

  Clock clock_1 (.out(clock_1_out));
  random random_1 (.in_1(clock_1_out), .out_2(random_1_out_2));
  // cdm16 cdm16_1: pin names not known; wires that end beside it: r0, r1, cdm16_1_p3, r2, r3, r4, r5, r6, r7, cdm16_1_p10, cdm16_1_p10, cdm16_1_p12, cdm16_1_p12, cdm16_1_p14, cdm16_1_p14, mem, read, word, address_bus, cdm16_1_p20, cdm16_1_p21
  Clock clock_2 (.out(cdm16_1_p3));
  Multiplexer #(.width(16), .enable("false")) multiplexer_1 (
    .in0(data_bus), .in1(random_1_out_2), .out(data), .sel(comparator_1_eq));
  Comparator #(.width(16)) comparator_1 (.a(16'hfefe), .b(address_bus), .eq(comparator_1_eq));  // open: gt, lt
  assign data_bus = not_1_out ? cdm16_1_p20 : 16'bz;  // Controlled_Buffer controlled_buffer_1
  not not_1 (not_1_out, read);
  Controlled_Buffer #(.width(16)) controlled_buffer_2 (.in(data_bus), .en(read));  // open: out
  assign cdm16_1_p21 = read ? data : 16'bz;  // Controlled_Buffer controlled_buffer_3
  DotMatrix #(.matrixcols(19), .matrixrows(19)) dotmatrix_1 (
    .col0({19{1'b1}}), .col1({19{1'b1}}), .col2({19{1'b1}}), .col3({19{1'b1}}), .col4({19{1'b0}}),
    .col5({19{1'b1}}), .col6({19{1'b1}}), .col7({19{1'b1}}), .col8({19{1'b1}}), .col9({19{1'b0}}),
    .col10({19{1'b1}}), .col11({19{1'b1}}), .col12({19{1'b1}}), .col13({19{1'b1}}), .col14({19{1'b0}}),
    .col15({19{1'b1}}), .col16({19{1'b1}}), .col17({19{1'b1}}), .col18({19{1'b1}}));
  DotMatrix #(.matrixcols(19), .matrixrows(19)) dotmatrix_2 (
    .col0({19{1'b1}}), .col1({19{1'b1}}), .col2({19{1'b1}}), .col3({19{1'b1}}), .col4({19{1'b0}}),
    .col5({19{1'b1}}), .col6({19{1'b1}}), .col7({19{1'b1}}), .col8({19{1'b1}}), .col9({19{1'b0}}),
    .col10({19{1'b1}}), .col11({19{1'b1}}), .col12({19{1'b1}}), .col13({19{1'b1}}), .col14({19{1'b0}}),
    .col15({19{1'b1}}), .col16({19{1'b1}}), .col17({19{1'b1}}), .col18({19{1'b1}}));
  DotMatrix #(.matrixcols(19), .matrixrows(19)) dotmatrix_3 (
    .col0({19{1'b1}}), .col1({19{1'b1}}), .col2({19{1'b1}}), .col3({19{1'b1}}), .col4({19{1'b0}}),
    .col5({19{1'b1}}), .col6({19{1'b1}}), .col7({19{1'b1}}), .col8({19{1'b1}}), .col9({19{1'b0}}),
    .col10({19{1'b1}}), .col11({19{1'b1}}), .col12({19{1'b1}}), .col13({19{1'b1}}), .col14({19{1'b0}}),
    .col15({19{1'b1}}), .col16({19{1'b1}}), .col17({19{1'b1}}), .col18({19{1'b1}}));
  DotMatrix #(.matrixcols(19), .matrixrows(19)) dotmatrix_4 (
    .col0({19{1'b1}}), .col1({19{1'b1}}), .col2({19{1'b1}}), .col3({19{1'b1}}), .col4({19{1'b0}}),
    .col5({19{1'b1}}), .col6({19{1'b1}}), .col7({19{1'b1}}), .col8({19{1'b1}}), .col9({19{1'b0}}),
    .col10({19{1'b1}}), .col11({19{1'b1}}), .col12({19{1'b1}}), .col13({19{1'b1}}), .col14({19{1'b0}}),
    .col15({19{1'b1}}), .col16({19{1'b1}}), .col17({19{1'b1}}), .col18({19{1'b1}}));
  DotMatrix #(.matrixcols(19), .matrixrows(19)) dotmatrix_5 (
    .col0({19{1'b1}}), .col1({19{1'b1}}), .col2({19{1'b1}}), .col3({19{1'b1}}), .col4({19{1'b0}}),
    .col5({19{1'b1}}), .col6({19{1'b1}}), .col7({19{1'b1}}), .col8({19{1'b1}}), .col9({19{1'b0}}),
    .col10({19{1'b1}}), .col11({19{1'b1}}), .col12({19{1'b1}}), .col13({19{1'b1}}), .col14({19{1'b0}}),
    .col15({19{1'b1}}), .col16({19{1'b1}}), .col17({19{1'b1}}), .col18({19{1'b1}}));
  DotMatrix #(.matrixcols(19), .matrixrows(19)) dotmatrix_6 (
    .col0({19{1'b1}}), .col1({19{1'b1}}), .col2({19{1'b1}}), .col3({19{1'b1}}), .col4({19{1'b0}}),
    .col5({19{1'b1}}), .col6({19{1'b1}}), .col7({19{1'b1}}), .col8({19{1'b1}}), .col9({19{1'b0}}),
    .col10({19{1'b1}}), .col11({19{1'b1}}), .col12({19{1'b1}}), .col13({19{1'b1}}), .col14({19{1'b0}}),
    .col15({19{1'b1}}), .col16({19{1'b1}}), .col17({19{1'b1}}), .col18({19{1'b1}}));
  DotMatrix #(.matrixcols(19), .matrixrows(19)) dotmatrix_7 (
    .col0({19{1'b1}}), .col1({19{1'b1}}), .col2({19{1'b1}}), .col3({19{1'b1}}), .col4({19{1'b0}}),
    .col5({19{1'b1}}), .col6({19{1'b1}}), .col7({19{1'b1}}), .col8({19{1'b1}}), .col9({19{1'b0}}),
    .col10({19{1'b1}}), .col11({19{1'b1}}), .col12({19{1'b1}}), .col13({19{1'b1}}), .col14({19{1'b0}}),
    .col15({19{1'b1}}), .col16({19{1'b1}}), .col17({19{1'b1}}), .col18({19{1'b1}}));
  DotMatrix #(.matrixcols(19), .matrixrows(19)) dotmatrix_8 (
    .col0({19{1'b1}}), .col1({19{1'b1}}), .col2({19{1'b1}}), .col3({19{1'b1}}), .col4({19{1'b0}}),
    .col5({19{1'b1}}), .col6({19{1'b1}}), .col7({19{1'b1}}), .col8({19{1'b1}}), .col9({19{1'b0}}),
    .col10({19{1'b1}}), .col11({19{1'b1}}), .col12({19{1'b1}}), .col13({19{1'b1}}), .col14({19{1'b0}}),
    .col15({19{1'b1}}), .col16({19{1'b1}}), .col17({19{1'b1}}), .col18({19{1'b1}}));
  Clock clock_3 (.out(clock_3_out));
  // Debugger debugger_1: pin names not known
  // RAM ram_1: pin names not known; wires that end beside it: address_bus, word, mem, clock_3_out, read, data_bus
  DotMatrix #(.matrixcols(19), .matrixrows(19)) dotmatrix_9 (
    .col0({19{1'b1}}), .col1({19{1'b1}}), .col2({19{1'b1}}), .col3({19{1'b1}}), .col4({19{1'b0}}),
    .col5({19{1'b1}}), .col6({19{1'b1}}), .col7({19{1'b1}}), .col8({19{1'b1}}), .col9({19{1'b0}}),
    .col10({19{1'b1}}), .col11({19{1'b1}}), .col12({19{1'b1}}), .col13({19{1'b1}}), .col14({19{1'b0}}),
    .col15({19{1'b1}}), .col16({19{1'b1}}), .col17({19{1'b1}}), .col18({19{1'b1}}));
  DotMatrix #(.matrixcols(19), .matrixrows(19)) dotmatrix_10 (
    .col0({19{1'b1}}), .col1({19{1'b1}}), .col2({19{1'b1}}), .col3({19{1'b1}}), .col4({19{1'b0}}),
    .col5({19{1'b1}}), .col6({19{1'b1}}), .col7({19{1'b1}}), .col8({19{1'b1}}), .col9({19{1'b0}}),
    .col10({19{1'b1}}), .col11({19{1'b1}}), .col12({19{1'b1}}), .col13({19{1'b1}}), .col14({19{1'b0}}),
    .col15({19{1'b1}}), .col16({19{1'b1}}), .col17({19{1'b1}}), .col18({19{1'b1}}));
  DotMatrix #(.matrixcols(19), .matrixrows(19)) dotmatrix_11 (
    .col0({19{1'b1}}), .col1({19{1'b1}}), .col2({19{1'b1}}), .col3({19{1'b1}}), .col4({19{1'b0}}),
    .col5({19{1'b1}}), .col6({19{1'b1}}), .col7({19{1'b1}}), .col8({19{1'b1}}), .col9({19{1'b0}}),
    .col10({19{1'b1}}), .col11({19{1'b1}}), .col12({19{1'b1}}), .col13({19{1'b1}}), .col14({19{1'b0}}),
    .col15({19{1'b1}}), .col16({19{1'b1}}), .col17({19{1'b1}}), .col18({19{1'b1}}));
  DotMatrix #(.matrixcols(19), .matrixrows(19)) dotmatrix_12 (
    .col0({19{1'b1}}), .col1({19{1'b1}}), .col2({19{1'b1}}), .col3({19{1'b1}}), .col4({19{1'b0}}),
    .col5({19{1'b1}}), .col6({19{1'b1}}), .col7({19{1'b1}}), .col8({19{1'b1}}), .col9({19{1'b0}}),
    .col10({19{1'b1}}), .col11({19{1'b1}}), .col12({19{1'b1}}), .col13({19{1'b1}}), .col14({19{1'b0}}),
    .col15({19{1'b1}}), .col16({19{1'b1}}), .col17({19{1'b1}}), .col18({19{1'b1}}));
  DotMatrix #(.matrixcols(19), .matrixrows(19)) dotmatrix_13 (
    .col0({19{1'b1}}), .col1({19{1'b1}}), .col2({19{1'b1}}), .col3({19{1'b1}}), .col4({19{1'b0}}),
    .col5({19{1'b1}}), .col6({19{1'b1}}), .col7({19{1'b1}}), .col8({19{1'b1}}), .col9({19{1'b0}}),
    .col10({19{1'b1}}), .col11({19{1'b1}}), .col12({19{1'b1}}), .col13({19{1'b1}}), .col14({19{1'b0}}),
    .col15({19{1'b1}}), .col16({19{1'b1}}), .col17({19{1'b1}}), .col18({19{1'b1}}));
  Hex_Digit_Display hex_digit_display_1 ();  // open: value, dp
  Hex_Digit_Display hex_digit_display_2 ();  // open: value, dp
  Hex_Digit_Display hex_digit_display_3 ();  // open: value, dp
  DotMatrix #(.matrixcols(19), .matrixrows(19)) dotmatrix_14 (
    .col0({19{1'b1}}), .col1({19{1'b1}}), .col2({19{1'b1}}), .col3({19{1'b1}}), .col4({19{1'b0}}),
    .col5({19{1'b1}}), .col6({19{1'b1}}), .col7({19{1'b1}}), .col8({19{1'b1}}), .col9({19{1'b0}}),
    .col10({19{1'b1}}), .col11({19{1'b1}}), .col12({19{1'b1}}), .col13({19{1'b1}}), .col14({19{1'b0}}),
    .col15({19{1'b1}}), .col16({19{1'b1}}), .col17({19{1'b1}}), .col18({19{1'b1}}));
  DotMatrix #(.matrixcols(19), .matrixrows(19)) dotmatrix_15 (
    .col0({19{1'b1}}), .col1({19{1'b1}}), .col2({19{1'b1}}), .col3({19{1'b1}}), .col4({19{1'b0}}),
    .col5({19{1'b1}}), .col6({19{1'b1}}), .col7({19{1'b1}}), .col8({19{1'b1}}), .col9({19{1'b0}}),
    .col10({19{1'b1}}), .col11({19{1'b1}}), .col12({19{1'b1}}), .col13({19{1'b1}}), .col14({19{1'b0}}),
    .col15({19{1'b1}}), .col16({19{1'b1}}), .col17({19{1'b1}}), .col18({19{1'b1}}));
  DotMatrix #(.matrixcols(19), .matrixrows(19)) dotmatrix_16 (
    .col0({19{1'b1}}), .col1({19{1'b1}}), .col2({19{1'b1}}), .col3({19{1'b1}}), .col4({19{1'b0}}),
    .col5({19{1'b1}}), .col6({19{1'b1}}), .col7({19{1'b1}}), .col8({19{1'b1}}), .col9({19{1'b0}}),
    .col10({19{1'b1}}), .col11({19{1'b1}}), .col12({19{1'b1}}), .col13({19{1'b1}}), .col14({19{1'b0}}),
    .col15({19{1'b1}}), .col16({19{1'b1}}), .col17({19{1'b1}}), .col18({19{1'b1}}));
  DotMatrix #(.matrixcols(19), .matrixrows(19)) dotmatrix_17 (
    .col0({19{1'b1}}), .col1({19{1'b1}}), .col2({19{1'b1}}), .col3({19{1'b1}}), .col4({19{1'b0}}),
    .col5({19{1'b1}}), .col6({19{1'b1}}), .col7({19{1'b1}}), .col8({19{1'b1}}), .col9({19{1'b0}}),
    .col10({19{1'b1}}), .col11({19{1'b1}}), .col12({19{1'b1}}), .col13({19{1'b1}}), .col14({19{1'b0}}),
    .col15({19{1'b1}}), .col16({19{1'b1}}), .col17({19{1'b1}}), .col18({19{1'b1}}));
  Hex_Digit_Display hex_digit_display_4 ();  // open: value, dp
  Hex_Digit_Display hex_digit_display_5 ();  // open: value, dp
  Button button_1 ();  // open: out
  Button button_2 ();  // open: out
  Button button_3 ();  // open: out
  // Probe on 19'hf80
  Button button_4 ();  // open: out
  DotMatrix #(.matrixcols(19), .matrixrows(19)) dotmatrix_18 (
    .col0(19'hf80), .col1(19'h1040), .col2(19'h1040), .col3(19'hf80), .col4({19{1'b0}}), .col5(undriven),
    .col6(undriven), .col7(undriven), .col8(undriven), .col9({19{1'b0}}), .col10(undriven), .col11(undriven),
    .col12(undriven), .col13(undriven), .col14({19{1'b0}}), .col15(undriven), .col16(undriven),
    .col17(undriven), .col18(undriven));

  // Other names for the same wires on the sheet: RAM[15:0] = data_bus

  // Notes on the sheet:
  //   Garvard architecture
  //   instructions memory
  //   there should be img-file
  //   data memory
  //   workspace
  //   счет
  //   сколько у нас памяти?
  //   как это стыкуется с процессором
  //   CONTROL PANEL
  //   (maybe make  a scheme for that)
endmodule

module random (
  input  in_1,
  output [15:0] out_2
);

  Random #(.width(4)) random_1 (.clk(in_1), .out(out_2[3:0]));  // open: next, clr

  assign out_2[15:4] = {12{1'b0}};
endmodule
